# Fritzing sketch ZoneController (saved by Fritzing 0.9.3b)
circuit board: 8.46667cm x 5.64444cm
breadboards: 1
stripboards: 1

parts:
  Part1 = Arduino Uno (Rev3)
  D1 = Diode [package=diode-1n4148]
  D2 = Diode [package=diode-1n4148]
  D3 = Diode [package=diode-1n4148]
  D4 = Diode [package=diode-1n4148]
  D5 = Diode [package=diode-1n4148]
  R1 = Resistor [tolerance=±5% resistance=10k package=THT]
  J1 = male pin header, 8 pins [form="♂ (male)"]
  R2 = Resistor [tolerance=±5% resistance=4.7 package=THT]
  Raspberry_Pi_B_rev1 = Raspberry Pi B rev1  # not connected

nets:
  N1: Part1.D10_PWM/SS, R1.Pin_0
  N2: Part1.GND, J1.pin1
  N3: Part1.D2, R2.Pin_0
  N4: Part1.D3_PWM, D5.A
  N5: Part1.D4, D4.A
  N6: Part1.D5_PWM, D3.A
  N7: Part1.D6_PWM, D2.A
  N8: Part1.D7, D1.A
  N9: D1.C, J1.pin3
  N10: D2.C, J1.pin4
  N11: D3.C, J1.pin5
  N12: D4.C, J1.pin6
  N13: D5.C, J1.pin7
  N14: R1.Pin_1, J1.pin2
  N15: J1.pin8, R2.Pin_1

notes:
  Wall Controller PCB Connections
